// Logisim project control-logic.circ as structural Verilog: 1 circuit, main circuit control_logic
module control_logic (
  input  [31:0] Instruction,
  input  BrEq,
  input  BrLt,
  output PCSel,
  output RegWEn,
  output [2:0] ImmSel,
  output BrUn,
  output ASel,
  output BSel,
  output [3:0] ALUSel,
  output MemWEn,
  output [1:0] WBSel
);

  wire and_14_out, and_15_out, and_16_out, and_17_out, and_18_out, and_19_out, and_20_out, comparator_10_eq,
       comparator_11_eq, comparator_12_eq, comparator_13_eq, comparator_14_eq, comparator_15_eq,
       comparator_16_eq, comparator_17_eq, comparator_18_eq, comparator_19_eq, comparator_20_eq,
       comparator_21_eq, comparator_22_eq, comparator_23_eq, comparator_24_eq, comparator_25_eq,
       comparator_26_eq, comparator_27_eq, comparator_28_eq, comparator_29_eq, comparator_30_eq,
       comparator_31_eq, comparator_32_eq, comparator_33_eq, comparator_34_eq, isAdd, isAnd, isAuipc,
       isBType, isIType, isJal, isJalr, isLoad, isLui, isMul, isMulh, isMulhu, isOr, isRType, isSll, isSlt,
       isSra, isSrl, isStore, isSub, isXor, multiplexer_6_out, multiplexer_7_out, multiplexer_8_out,
       multiplexer_11_out, multiplexer_13_out, multiplexer_14_out, multiplexer_15_out, multiplexer_18_out,
       multiplexer_20_out, multiplexer_21_out, multiplexer_22_out, multiplexer_25_out, multiplexer_28_out,
       multiplexer_29_out, multiplexer_30_out, multiplexer_33_out, multiplexer_35_out, multiplexer_36_out,
       multiplexer_37_out, multiplexer_40_out, multiplexer_42_out, multiplexer_43_out, multiplexer_44_out,
       multiplexer_47_out, multiplexer_49_out, multiplexer_50_out, multiplexer_51_out, multiplexer_54_out,
       multiplexer_55_out, multiplexer_56_out, multiplexer_57_out, multiplexer_60_out, not_1_out, not_2_out,
       not_3_out, not_4_out, not_5_out, or_1_out, or_2_out, or_3_out, or_4_out, or_5_out, or_6_out, or_7_out,
       or_8_out, or_9_out;
  wire [1:0] multiplexer_10_out, multiplexer_17_out, multiplexer_24_out, multiplexer_32_out,
       multiplexer_39_out, multiplexer_46_out, multiplexer_53_out, multiplexer_59_out;
  wire [2:0] multiplexer_9_out, multiplexer_16_out, multiplexer_23_out, multiplexer_31_out,
       multiplexer_38_out, multiplexer_45_out, multiplexer_52_out;
  wire [3:0] multiplexer_1_out, multiplexer_2_out, multiplexer_3_out, multiplexer_4_out, multiplexer_5_out,
       multiplexer_12_out, multiplexer_19_out, multiplexer_26_out, multiplexer_27_out, multiplexer_34_out,
       multiplexer_41_out;
  wire [15:0] rom_1_data;

  Multiplexer #(.width(4)) multiplexer_1 (.in0(4'b0000), .in1(4'b0000), .out(multiplexer_1_out), .sel(isAdd));
  Multiplexer #(.width(4)) multiplexer_2 (.in0(multiplexer_1_out), .in1(4'b0111), .out(multiplexer_2_out), .sel(isAnd));
  Comparator #(.width(7)) comparator_1 (.a(Instruction[6:0]), .b(7'b0010011), .eq(isIType));  // open: gt, lt
  Comparator #(.width(7)) comparator_2 (.a(Instruction[6:0]), .b(7'b0110011), .eq(isRType));  // open: gt, lt
  Comparator #(.width(7)) comparator_3 (.a(Instruction[6:0]), .b(7'b1100011), .eq(isBType));  // open: gt, lt
  Comparator #(.width(7)) comparator_4 (.a(Instruction[6:0]), .b(7'b0000011), .eq(isLoad));  // open: gt, lt
  Comparator #(.width(7)) comparator_5 (.a(Instruction[6:0]), .b(7'b0100011), .eq(isStore));  // open: gt, lt
  Comparator #(.width(7)) comparator_6 (.a(Instruction[6:0]), .b(7'b1101111), .eq(isJal));  // open: gt, lt
  Comparator #(.width(7)) comparator_7 (.a(Instruction[6:0]), .b(7'b1100111), .eq(isJalr));  // open: gt, lt
  Comparator #(.width(7)) comparator_8 (.a(Instruction[6:0]), .b(7'b0010111), .eq(isAuipc));  // open: gt, lt
  Comparator #(.width(7)) comparator_9 (.a(Instruction[6:0]), .b(7'b0110111), .eq(isLui));  // open: gt, lt
  Multiplexer #(.width(4)) multiplexer_3 (.in0(multiplexer_2_out), .in1(4'b0110), .out(multiplexer_3_out), .sel(isOr));
  Comparator #(.width(3)) comparator_10 (.a(Instruction[14:12]), .b(3'b000), .eq(comparator_10_eq));  // open: gt, lt
  Comparator #(.width(3)) comparator_11 (.a(Instruction[14:12]), .b(3'b111), .eq(comparator_11_eq));  // open: gt, lt
  Comparator #(.width(3)) comparator_12 (.a(Instruction[14:12]), .b(3'b110), .eq(comparator_12_eq));  // open: gt, lt
  Comparator #(.width(3)) comparator_13 (.a(Instruction[14:12]), .b(3'b100), .eq(comparator_13_eq));  // open: gt, lt
  Comparator #(.width(7)) comparator_14 (.a(Instruction[31:25]), .b({7{1'b0}}), .eq(comparator_14_eq));  // open: gt, lt
  Comparator #(.width(3)) comparator_15 (.a(Instruction[14:12]), .b(3'b001), .eq(comparator_15_eq));  // open: gt, lt
  Comparator #(.width(7)) comparator_16 (.a(Instruction[31:25]), .b({7{1'b0}}), .eq(comparator_16_eq));  // open: gt, lt
  Comparator #(.width(3)) comparator_17 (.a(Instruction[14:12]), .b(3'b101), .eq(comparator_17_eq));  // open: gt, lt
  Comparator #(.width(7)) comparator_18 (
    .a(Instruction[31:25]), .b(7'b0100000), .eq(comparator_18_eq));  // open: gt, lt
  Comparator #(.width(3)) comparator_19 (.a(Instruction[14:12]), .b(3'b101), .eq(comparator_19_eq));  // open: gt, lt
  Comparator #(.width(3)) comparator_20 (.a(Instruction[14:12]), .b(3'b010), .eq(comparator_20_eq));  // open: gt, lt
  Comparator #(.width(7)) comparator_21 (
    .a(Instruction[31:25]), .b(7'b0000001), .eq(comparator_21_eq));  // open: gt, lt
  Comparator #(.width(3)) comparator_22 (.a(Instruction[14:12]), .b(3'b000), .eq(comparator_22_eq));  // open: gt, lt
  Comparator #(.width(7)) comparator_23 (
    .a(Instruction[31:25]), .b(7'b0000001), .eq(comparator_23_eq));  // open: gt, lt
  Comparator #(.width(3)) comparator_24 (.a(Instruction[14:12]), .b(3'b001), .eq(comparator_24_eq));  // open: gt, lt
  Comparator #(.width(7)) comparator_25 (
    .a(Instruction[31:25]), .b(7'b0000001), .eq(comparator_25_eq));  // open: gt, lt
  Comparator #(.width(3)) comparator_26 (.a(Instruction[14:12]), .b(3'b011), .eq(comparator_26_eq));  // open: gt, lt
  Comparator #(.width(7)) comparator_27 (
    .a(Instruction[31:25]), .b(7'b0100000), .eq(comparator_27_eq));  // open: gt, lt
  Comparator #(.width(3)) comparator_28 (.a(Instruction[14:12]), .b(3'b000), .eq(comparator_28_eq));  // open: gt, lt
  Multiplexer #(.width(4)) multiplexer_4 (.in0(multiplexer_3_out), .in1(4'b0100), .out(multiplexer_4_out), .sel(isXor));
  Multiplexer #(.width(4)) multiplexer_5 (.in0(multiplexer_4_out), .in1(4'b0001), .out(multiplexer_5_out), .sel(isSll));
  Multiplexer multiplexer_6 (.in0(1'b0), .in1(1'b1), .out(multiplexer_6_out), .sel(isIType));
  Multiplexer multiplexer_7 (.in0(1'b0), .in1(1'b0), .out(multiplexer_7_out), .sel(isIType));
  Multiplexer multiplexer_8 (.in0(1'b0), .in1(1'b0), .out(multiplexer_8_out), .sel(isIType));
  Multiplexer #(.width(3)) multiplexer_9 (.in0(3'b000), .in1(3'b000), .out(multiplexer_9_out), .sel(isIType));
  Multiplexer #(.width(2)) multiplexer_10 (.in0(2'b00), .in1(2'b00), .out(multiplexer_10_out), .sel(isIType));
  Multiplexer multiplexer_11 (.in0(1'b0), .in1(1'b0), .out(multiplexer_11_out), .sel(isIType));
  Multiplexer #(.width(4)) multiplexer_12 (
    .in0(multiplexer_5_out), .in1(4'b0101), .out(multiplexer_12_out), .sel(isSrl));
  or or_1 (or_1_out, isIType, isRType, isLoad, isStore, isJal, isJalr, isAuipc, isLui);
  or or_2 (or_2_out, isIType, isRType);
  or or_3 (or_3_out, isIType, isRType);
  or or_4 (or_4_out, isIType, isRType);
  or or_5 (or_5_out, isIType, isRType);
  or or_6 (or_6_out, isIType, isRType);
  or or_7 (or_7_out, isIType, isRType);
  or or_8 (or_8_out, isIType, isRType);
  Multiplexer multiplexer_13 (.in0(multiplexer_6_out), .in1(1'b1), .out(multiplexer_13_out), .sel(isRType));
  Multiplexer multiplexer_14 (.in0(multiplexer_7_out), .in1(1'b1), .out(multiplexer_14_out), .sel(isRType));
  Multiplexer multiplexer_15 (.in0(multiplexer_8_out), .in1(1'b0), .out(multiplexer_15_out), .sel(isRType));
  Multiplexer #(.width(3)) multiplexer_16 (
    .in0(multiplexer_9_out), .in1(3'b010), .out(multiplexer_16_out), .sel(isBType));
  Multiplexer #(.width(2)) multiplexer_17 (
    .in0(multiplexer_10_out), .in1(2'b00), .out(multiplexer_17_out), .sel(isRType));
  Multiplexer multiplexer_18 (.in0(multiplexer_11_out), .in1(1'b0), .out(multiplexer_18_out), .sel(isRType));
  Multiplexer #(.width(4)) multiplexer_19 (
    .in0(multiplexer_12_out), .in1(4'b1101), .out(multiplexer_19_out), .sel(isSra));
  and and_1 (isAdd, comparator_10_eq, or_1_out);
  and and_2 (isAnd, comparator_11_eq, or_2_out);
  and and_3 (isOr, comparator_12_eq, or_3_out);
  and and_4 (isXor, comparator_13_eq, or_4_out);
  and and_5 (isSll, comparator_14_eq, comparator_15_eq, or_5_out);
  and and_6 (isSrl, comparator_16_eq, comparator_17_eq, or_6_out);
  and and_7 (isSra, comparator_18_eq, comparator_19_eq, or_7_out);
  and and_8 (isSlt, comparator_20_eq, or_8_out);
  and and_9 (isMul, comparator_21_eq, comparator_22_eq, isRType);
  and and_10 (isMulh, comparator_23_eq, comparator_24_eq, isRType);
  and and_11 (isMulhu, comparator_25_eq, comparator_26_eq, isRType);
  and and_12 (isSub, comparator_27_eq, comparator_28_eq, isRType);
  Multiplexer multiplexer_20 (.in0(multiplexer_13_out), .in1(1'b0), .out(multiplexer_20_out), .sel(isBType));
  Multiplexer multiplexer_21 (.in0(multiplexer_14_out), .in1(1'b0), .out(multiplexer_21_out), .sel(isLoad));
  Multiplexer multiplexer_22 (.in0(multiplexer_15_out), .in1(1'b1), .out(multiplexer_22_out), .sel(isBType));
  Multiplexer #(.width(3)) multiplexer_23 (
    .in0(multiplexer_16_out), .in1(3'b000), .out(multiplexer_23_out), .sel(isLoad));
  Multiplexer #(.width(2)) multiplexer_24 (
    .in0(multiplexer_17_out), .in1(2'b00), .out(multiplexer_24_out), .sel(isBType));
  Multiplexer multiplexer_25 (.in0(multiplexer_18_out), .in1(1'b0), .out(multiplexer_25_out), .sel(isBType));
  Multiplexer #(.width(4)) multiplexer_26 (
    .in0(multiplexer_19_out), .in1(4'b0010), .out(multiplexer_26_out), .sel(isSlt));
  Multiplexer #(.width(4)) multiplexer_27 (
    .in0(multiplexer_26_out), .in1(4'b1000), .out(multiplexer_27_out), .sel(isMul));
  Multiplexer multiplexer_28 (.in0(multiplexer_20_out), .in1(1'b1), .out(multiplexer_28_out), .sel(isLoad));
  Multiplexer multiplexer_29 (.in0(multiplexer_21_out), .in1(1'b0), .out(multiplexer_29_out), .sel(isStore));
  Multiplexer multiplexer_30 (.in0(multiplexer_22_out), .in1(1'b0), .out(multiplexer_30_out), .sel(isLoad));
  Multiplexer #(.width(3)) multiplexer_31 (
    .in0(multiplexer_23_out), .in1(3'b001), .out(multiplexer_31_out), .sel(isStore));
  Multiplexer #(.width(2)) multiplexer_32 (
    .in0(multiplexer_24_out), .in1(2'b01), .out(multiplexer_32_out), .sel(isLoad));
  Multiplexer multiplexer_33 (.in0(multiplexer_25_out), .in1(1'b0), .out(multiplexer_33_out), .sel(isLoad));
  Multiplexer #(.width(4)) multiplexer_34 (
    .in0(multiplexer_27_out), .in1(4'b1001), .out(multiplexer_34_out), .sel(isMulh));
  Multiplexer multiplexer_35 (.in0(multiplexer_28_out), .in1(1'b0), .out(multiplexer_35_out), .sel(isStore));
  Multiplexer multiplexer_36 (.in0(multiplexer_29_out), .in1(1'b0), .out(multiplexer_36_out), .sel(isBType));
  Multiplexer multiplexer_37 (.in0(multiplexer_30_out), .in1(1'b0), .out(multiplexer_37_out), .sel(isStore));
  Multiplexer #(.width(3)) multiplexer_38 (
    .in0(multiplexer_31_out), .in1(3'b100), .out(multiplexer_38_out), .sel(isJal));
  Multiplexer #(.width(2)) multiplexer_39 (
    .in0(multiplexer_32_out), .in1(2'b10), .out(multiplexer_39_out), .sel(isStore));
  Multiplexer multiplexer_40 (.in0(multiplexer_33_out), .in1(1'b1), .out(multiplexer_40_out), .sel(isStore));
  Multiplexer #(.width(4)) multiplexer_41 (
    .in0(multiplexer_34_out), .in1(4'b1011), .out(multiplexer_41_out), .sel(isMulhu));
  Multiplexer multiplexer_42 (.in0(multiplexer_35_out), .in1(1'b1), .out(multiplexer_42_out), .sel(isJal));
  Multiplexer multiplexer_43 (.in0(multiplexer_36_out), .in1(1'b0), .out(multiplexer_43_out), .sel(isJal));
  Multiplexer multiplexer_44 (.in0(multiplexer_37_out), .in1(1'b1), .out(multiplexer_44_out), .sel(isJal));
  Multiplexer #(.width(3)) multiplexer_45 (
    .in0(multiplexer_38_out), .in1(3'b000), .out(multiplexer_45_out), .sel(isJalr));
  Multiplexer #(.width(2)) multiplexer_46 (
    .in0(multiplexer_39_out), .in1(2'b11), .out(multiplexer_46_out), .sel(isJal));
  Multiplexer multiplexer_47 (.in0(multiplexer_40_out), .in1(1'b0), .out(multiplexer_47_out), .sel(isJal));
  Multiplexer #(.width(4)) multiplexer_48 (.in0(multiplexer_41_out), .in1(4'b1100), .out(ALUSel), .sel(isSub));
  Multiplexer multiplexer_49 (.in0(multiplexer_42_out), .in1(1'b1), .out(multiplexer_49_out), .sel(isJalr));
  Multiplexer multiplexer_50 (.in0(multiplexer_43_out), .in1(1'b0), .out(multiplexer_50_out), .sel(isJalr));
  Multiplexer multiplexer_51 (.in0(multiplexer_44_out), .in1(1'b0), .out(multiplexer_51_out), .sel(isJalr));
  Multiplexer #(.width(3)) multiplexer_52 (
    .in0(multiplexer_45_out), .in1(3'b011), .out(multiplexer_52_out), .sel(isAuipc));
  Multiplexer #(.width(2)) multiplexer_53 (
    .in0(multiplexer_46_out), .in1(2'b11), .out(multiplexer_53_out), .sel(isJalr));
  Multiplexer multiplexer_54 (.in0(multiplexer_47_out), .in1(1'b0), .out(multiplexer_54_out), .sel(isJalr));
  Comparator #(.width(3)) comparator_29 (.a(Instruction[14:12]), .b(3'b000), .eq(comparator_29_eq));  // open: gt, lt
  Comparator #(.width(3)) comparator_30 (.a(Instruction[14:12]), .b(3'b101), .eq(comparator_30_eq));  // open: gt, lt
  Comparator #(.width(3)) comparator_31 (.a(Instruction[14:12]), .b(3'b111), .eq(comparator_31_eq));  // open: gt, lt
  Comparator #(.width(3)) comparator_32 (.a(Instruction[14:12]), .b(3'b100), .eq(comparator_32_eq));  // open: gt, lt
  Comparator #(.width(3)) comparator_33 (.a(Instruction[14:12]), .b(3'b110), .eq(comparator_33_eq));  // open: gt, lt
  Comparator #(.width(3)) comparator_34 (.a(Instruction[14:12]), .b(3'b001), .eq(comparator_34_eq));  // open: gt, lt
  Multiplexer multiplexer_55 (.in0(multiplexer_49_out), .in1(1'b1), .out(multiplexer_55_out), .sel(isAuipc));
  Multiplexer multiplexer_56 (.in0(multiplexer_50_out), .in1(1'b0), .out(multiplexer_56_out), .sel(isAuipc));
  Multiplexer multiplexer_57 (.in0(multiplexer_51_out), .in1(1'b1), .out(multiplexer_57_out), .sel(isAuipc));
  Multiplexer #(.width(3)) multiplexer_58 (.in0(multiplexer_52_out), .in1(3'b011), .out(ImmSel), .sel(isLui));
  Multiplexer #(.width(2)) multiplexer_59 (
    .in0(multiplexer_53_out), .in1(2'b00), .out(multiplexer_59_out), .sel(isAuipc));
  Multiplexer multiplexer_60 (.in0(multiplexer_54_out), .in1(1'b0), .out(multiplexer_60_out), .sel(isAuipc));
  not not_1 (not_1_out, comparator_30_eq);
  not not_2 (not_2_out, comparator_32_eq);
  Multiplexer multiplexer_61 (.in0(multiplexer_55_out), .in1(1'b1), .out(RegWEn), .sel(isLui));
  Multiplexer multiplexer_62 (.in0(multiplexer_56_out), .in1(1'b0), .out(BSel), .sel(isLui));
  Multiplexer multiplexer_63 (.in0(multiplexer_57_out), .in1(1'b0), .out(ASel), .sel(isLui));
  Multiplexer #(.width(2)) multiplexer_64 (.in0(multiplexer_59_out), .in1(2'b00), .out(WBSel), .sel(isLui));
  Multiplexer multiplexer_65 (.in0(multiplexer_60_out), .in1(1'b0), .out(MemWEn), .sel(isLui));
  and and_13 (BrUn, not_1_out, comparator_31_eq, not_2_out, comparator_33_eq);
  and and_14 (and_14_out, comparator_29_eq, BrEq);
  not not_3 (not_3_out, BrLt);
  not not_4 (not_4_out, BrLt);
  not not_5 (not_5_out, BrEq);
  ROM #(.addrWidth(6), .dataWidth(16)) rom_1 (.data(rom_1_data));  // open: addr
  and and_15 (and_15_out, comparator_30_eq, not_3_out);
  and and_16 (and_16_out, comparator_31_eq, not_4_out);
  and and_17 (and_17_out, comparator_32_eq, BrLt);
  and and_18 (and_18_out, comparator_33_eq, BrLt);
  and and_19 (and_19_out, comparator_34_eq, not_5_out);
  or or_9 (or_9_out, and_14_out, and_15_out, and_16_out, and_17_out, and_18_out, and_19_out);
  and and_20 (and_20_out, isBType, or_9_out);
  or or_10 (PCSel, and_20_out, isJal, isJalr);

  // Other names for the same wires on the sheet: Opcode[6:0] = Instruction[6:0]; Rd[4:0] = Instruction[11:7];
  //   Func3[2:0] = Instruction[14:12]; Rs1[4:0] = Instruction[19:15]; Rs2[4:0] = Instruction[24:20];
  //   Func7[6:0] = Instruction[31:25]

  // Notes on the sheet:
  //   INPUTS to your circuit
  //   DON'T CHANGE THE LOCATIONS OF THE INPUTS AND OUTPUTS!
  //   OUTPUT from your circuit
  //   Connect ROM Input here ->
  //   ROM FOR CONTROL LOGIC
  //   This is only if you choose to do the ROM option
  //   CONNECT
  //   WIRE
  //   TO
  //   USE
  //   ROM
  //   Reminder: If using ROM, use combinational logic for PCSel
endmodule
