// Logisim project partial-load.circ as structural Verilog: 1 circuit, main circuit partial_load
module partial_load (
  input  [31:0] Instruction,
  input  [31:0] MemAddress,
  input  [31:0] DataFromMem,
  output [31:0] DataToReg
);

  wire [31:0] bit_extender_1_out, bit_extender_2_out, bit_extender_3_out, bit_extender_4_out,
       bit_extender_5_out, bit_extender_6_out, bit_extender_7_out;

  assign bit_extender_1_out = {{24{DataFromMem[7]}}, DataFromMem[7:0]};  // Bit_Extender bit_extender_1
  assign bit_extender_2_out = {{24{DataFromMem[15]}}, DataFromMem[15:8]};  // Bit_Extender bit_extender_2
  assign bit_extender_3_out = {{24{DataFromMem[23]}}, DataFromMem[23:16]};  // Bit_Extender bit_extender_3
  assign bit_extender_4_out = {{24{DataFromMem[31]}}, DataFromMem[31:24]};  // Bit_Extender bit_extender_4
  assign bit_extender_5_out = {{16{DataFromMem[15]}}, DataFromMem[15:0]};  // Bit_Extender bit_extender_5
  assign bit_extender_6_out = {{16{DataFromMem[23]}}, DataFromMem[23:8]};  // Bit_Extender bit_extender_6
  assign bit_extender_7_out = {{16{DataFromMem[31]}}, DataFromMem[31:16]};  // Bit_Extender bit_extender_7
  Multiplexer #(.select(4), .width(32)) multiplexer_1 (
    .in0(bit_extender_1_out), .in1(bit_extender_2_out), .in2(bit_extender_3_out), .in3(bit_extender_4_out),
    .in4(bit_extender_5_out), .in5(bit_extender_6_out), .in6(bit_extender_7_out), .in8(DataFromMem),
    .out(DataToReg), .sel({Instruction[13:12], MemAddress[1:0]}));  // open: in7, in9, in10, in11, in12, in13, in14, in15

  // Other names for the same wires on the sheet: Opcode[6:0] = Instruction[6:0]; Rd[4:0] = Instruction[11:7];
  //   Func3[2:0] = Instruction[14:12]; Rs1[4:0] = Instruction[19:15]; Offset[11:0] = Instruction[31:20];
  //   LoadSel[3:0] = {Instruction[13:12], MemAddress[1:0]}

  // Notes on the sheet:
  //   INPUTS to your circuit
  //   DON'T CHANGE THE LOCATIONS OF THE INPUTS AND OUTPUTS!
  //   OUTPUT from your circuit
endmodule
